# Fritzing sketch Reloj_Temperatura_Humedad (saved by Fritzing 1.0.1rc)
circuit board: 8.46667cm x 5.64444cm
breadboards: 1

parts:
  DHT1 = DHT22 Humidity and Temperature Sensor
  U1 = ESP32-38PinWide [part_number=ESP32-38PinWide]
  LCM1602_IIC1 = LCM1602 IIC [part_number="LCM1602 IIC" chip_label="LCM1602 IIC" package="DIP (Dual Inline) [THT]"]
  LCD1 = 20x4 LCD display [part_number=2004A]
  R2 = Resistor [tolerance=±5% resistance=10k package="2010 [SMD]"]
  R1 = Photocell (LDR) [power=0.25W dark_resistance_@0.01lx=300kΩ light_resistance_@100lx=400Ω luminance=10lx package=THT]

nets (from the breadboard view):
  N1: DHT1.VDD, U1.3.3
  N2: DHT1.DATA, U1.GPIO27
  GND: DHT1.GND, U1.GND, LCM1602_IIC1.GND, R2.Pin_1
  N3: U1.GPIO32, R2.Pin_0, R1.pin_1
  N4: U1.VIN, R1.pin_0
  N5: U1.GPIO18, LCM1602_IIC1.LED_A
  N6: U1.GPIO21, LCM1602_IIC1.SDA
  N7: U1.GPIO22, LCM1602_IIC1.SCL
  VSS: LCM1602_IIC1.VSS, LCD1.Vss
  VDD: LCM1602_IIC1.VDD, LCD1.Vdd
  N8: LCM1602_IIC1.V0, LCD1.Vo
  N9: LCM1602_IIC1.RS, LCD1.RS
  N10: LCM1602_IIC1.RW, LCD1.R/W
  N11: LCM1602_IIC1.E, LCD1.E
  N12: LCM1602_IIC1.D0, LCD1.DB0
  N13: LCM1602_IIC1.D1, LCD1.DB1
  N14: LCM1602_IIC1.D2, LCD1.DB2
  N15: LCM1602_IIC1.D3, LCD1.DB3
  N16: LCM1602_IIC1.D4, LCD1.DB4
  N17: LCM1602_IIC1.D5, LCD1.DB5
  N18: LCM1602_IIC1.D6, LCD1.DB6
  N19: LCM1602_IIC1.D7, LCD1.DB7
  N20: LCM1602_IIC1.A, LCD1.A_+
  N21: LCM1602_IIC1.K, LCD1.K_-

custom parts:
  ESP32-38PinWide: Generic 38-Pin ESP32 with wide format (only access to one side of pins on a breadboard) based on Stephen Lilley's HiLetgo ESP-WROOM-32 ESP32 ESP-32S Development Board.
  LCM1602 IIC: I2C-Module to use a 1602 or 2004 LCD on with the wire.h libory Serial LCD Modul
  20x4 LCD display: 20x4 character display. CHECK LED POLARITY BEFORE CONNECTING POWER Some versions of the dispaly have the polarity of the LED pins "A" and "K" reversed.
